# Fritzing sketch touch-synth (saved by Fritzing 0.9.6b)
breadboards: 1

parts:
  R1 = Resistor [tolerance=±5% power=0.25 resistance=1M package=THT]
  R2 = Resistor [tolerance=±5% power=0.25 resistance=1M package=THT]
  R3 = Resistor [tolerance=±5% power=0.25 resistance=1M package=THT]
  SP1 = SPEAKER [package=pcb_mount_speaker]  # not connected

nets:
  N1: R1.Pin_1, R2.Pin_1, R3.Pin_1
